// Logisim project lab10part1.circ as structural Verilog: 4 circuits, main circuit main
module main (
  input  [3:0] INPUT
);

  wire clock_1_out, LockDetect_y;
  wire [1:0] PopCount_x0;
  wire [31:0] romsets_1_out_3, romsets_1_out_4, romsets_1_out_5, romsets_1_out_6, romsets_1_out_7,
       romsets_1_out_8, romsets_1_out_9, romsets_1_out_10, romsets_1_out_11, romsets_1_out_12,
       romsets_1_out_13, romsets_1_out_14, romsets_1_out_15, romsets_1_out_16, romsets_1_out_17,
       romsets_1_out_18, romsets_1_out_19, romsets_1_out_20, romsets_1_out_21, romsets_1_out_22,
       romsets_1_out_23, romsets_1_out_24, romsets_1_out_25, romsets_1_out_26, romsets_1_out_27,
       romsets_1_out_28, romsets_1_out_29, romsets_1_out_30, romsets_1_out_31, romsets_1_out_32,
       romsets_1_out_33, romsets_1_out_34;

  PopCount PopCount (.A(INPUT[3]), .B(INPUT[2]), .C(INPUT[1]), .D(INPUT[0]), .X1(PopCount_x0[1]), .X0(PopCount_x0[0]));
  LockDetect LockDetect (.A(INPUT[3]), .B(INPUT[2]), .C(INPUT[1]), .D(INPUT[0]), .Y(LockDetect_y));
  Hex_Digit_Display hex_digit_display_1 (.value({2'b00, PopCount_x0}));  // open: dp
  RomSets romsets_1 (
    .correct(LockDetect_y), .out_3(romsets_1_out_3), .out_4(romsets_1_out_4), .out_5(romsets_1_out_5),
    .out_6(romsets_1_out_6), .out_7(romsets_1_out_7), .out_8(romsets_1_out_8), .out_9(romsets_1_out_9),
    .out_10(romsets_1_out_10), .out_11(romsets_1_out_11), .out_12(romsets_1_out_12),
    .out_13(romsets_1_out_13), .out_14(romsets_1_out_14), .out_15(romsets_1_out_15),
    .out_16(romsets_1_out_16), .out_17(romsets_1_out_17), .out_18(romsets_1_out_18),
    .out_19(romsets_1_out_19), .out_20(romsets_1_out_20), .out_21(romsets_1_out_21),
    .out_22(romsets_1_out_22), .out_23(romsets_1_out_23), .out_24(romsets_1_out_24),
    .out_25(romsets_1_out_25), .out_26(romsets_1_out_26), .out_27(romsets_1_out_27),
    .out_28(romsets_1_out_28), .out_29(romsets_1_out_29), .out_30(romsets_1_out_30),
    .out_31(romsets_1_out_31), .out_32(romsets_1_out_32), .out_33(romsets_1_out_33),
    .out_34(romsets_1_out_34), .Clock(clock_1_out));
  DotMatrix #(.matrixcols(32), .matrixrows(32)) dotmatrix_1 (
    .col0(romsets_1_out_3), .col1(romsets_1_out_4), .col2(romsets_1_out_5), .col3(romsets_1_out_6),
    .col4(romsets_1_out_7), .col5(romsets_1_out_8), .col6(romsets_1_out_9), .col7(romsets_1_out_10),
    .col8(romsets_1_out_11), .col9(romsets_1_out_12), .col10(romsets_1_out_13), .col11(romsets_1_out_14),
    .col12(romsets_1_out_15), .col13(romsets_1_out_16), .col14(romsets_1_out_17), .col15(romsets_1_out_18),
    .col16(romsets_1_out_19), .col17(romsets_1_out_20), .col18(romsets_1_out_21), .col19(romsets_1_out_22),
    .col20(romsets_1_out_23), .col21(romsets_1_out_24), .col22(romsets_1_out_25), .col23(romsets_1_out_26),
    .col24(romsets_1_out_27), .col25(romsets_1_out_28), .col26(romsets_1_out_29), .col27(romsets_1_out_30),
    .col28(romsets_1_out_31), .col29(romsets_1_out_32), .col30(romsets_1_out_33), .col31(romsets_1_out_34));
  Clock clock_1 (.out(clock_1_out));
endmodule

module RomSets (
  input  correct,
  input  Clock,
  output [31:0] out_3,
  output [31:0] out_4,
  output [31:0] out_5,
  output [31:0] out_6,
  output [31:0] out_7,
  output [31:0] out_8,
  output [31:0] out_9,
  output [31:0] out_10,
  output [31:0] out_11,
  output [31:0] out_12,
  output [31:0] out_13,
  output [31:0] out_14,
  output [31:0] out_15,
  output [31:0] out_16,
  output [31:0] out_17,
  output [31:0] out_18,
  output [31:0] out_19,
  output [31:0] out_20,
  output [31:0] out_21,
  output [31:0] out_22,
  output [31:0] out_23,
  output [31:0] out_24,
  output [31:0] out_25,
  output [31:0] out_26,
  output [31:0] out_27,
  output [31:0] out_28,
  output [31:0] out_29,
  output [31:0] out_30,
  output [31:0] out_31,
  output [31:0] out_32,
  output [31:0] out_33,
  output [31:0] out_34
);

  wire and_1_out, not_1_out;
  wire [4:0] counter_1_q, multiplexer_1_out;

  Multiplexer #(.width(5)) multiplexer_1 (
    .in0({5{1'b0}}), .in1(counter_1_q), .out(multiplexer_1_out), .sel(correct));  // open: en
  and and_1 (and_1_out, correct, Clock);
  ROM #(.addrWidth(5), .dataWidth(32)) rom_1 (.addr(multiplexer_1_out), .data(out_3));  // open: sel
  ROM #(.addrWidth(5), .dataWidth(32)) rom_2 (.addr(multiplexer_1_out), .data(out_4));  // open: sel
  Counter #(.width(5), .max('h1), .ongoal("stay")) counter_1 (
    .Q(counter_1_q), .clk(and_1_out), .clr(not_1_out));  // open: load, D, count, carry
  not not_1 (not_1_out, correct);
  ROM #(.addrWidth(5), .dataWidth(32)) rom_3 (.addr(multiplexer_1_out), .data(out_5));  // open: sel
  ROM #(.addrWidth(5), .dataWidth(32)) rom_4 (.addr(multiplexer_1_out), .data(out_6));  // open: sel
  ROM #(.addrWidth(5), .dataWidth(32)) rom_5 (.addr(multiplexer_1_out), .data(out_7));  // open: sel
  ROM #(.addrWidth(5), .dataWidth(32)) rom_6 (.addr(multiplexer_1_out), .data(out_8));  // open: sel
  ROM #(.addrWidth(5), .dataWidth(32)) rom_7 (.addr(multiplexer_1_out), .data(out_9));  // open: sel
  ROM #(.addrWidth(5), .dataWidth(32)) rom_8 (.addr(multiplexer_1_out), .data(out_10));  // open: sel
  ROM #(.addrWidth(5), .dataWidth(32)) rom_9 (.addr(multiplexer_1_out), .data(out_11));  // open: sel
  ROM #(.addrWidth(5), .dataWidth(32)) rom_10 (.addr(multiplexer_1_out), .data(out_12));  // open: sel
  ROM #(.addrWidth(5), .dataWidth(32)) rom_11 (.addr(multiplexer_1_out), .data(out_13));  // open: sel
  ROM #(.addrWidth(5), .dataWidth(32)) rom_12 (.addr(multiplexer_1_out), .data(out_14));  // open: sel
  ROM #(.addrWidth(5), .dataWidth(32)) rom_13 (.addr(multiplexer_1_out), .data(out_15));  // open: sel
  ROM #(.addrWidth(5), .dataWidth(32)) rom_14 (.addr(multiplexer_1_out), .data(out_16));  // open: sel
  ROM #(.addrWidth(5), .dataWidth(32)) rom_15 (.addr(multiplexer_1_out), .data(out_17));  // open: sel
  ROM #(.addrWidth(5), .dataWidth(32)) rom_16 (.addr(multiplexer_1_out), .data(out_18));  // open: sel
  ROM #(.addrWidth(5), .dataWidth(32)) rom_17 (.addr(multiplexer_1_out), .data(out_19));  // open: sel
  ROM #(.addrWidth(5), .dataWidth(32)) rom_18 (.addr(multiplexer_1_out), .data(out_20));  // open: sel
  ROM #(.addrWidth(5), .dataWidth(32)) rom_19 (.addr(multiplexer_1_out), .data(out_21));  // open: sel
  ROM #(.addrWidth(5), .dataWidth(32)) rom_20 (.addr(multiplexer_1_out), .data(out_22));  // open: sel
  ROM #(.addrWidth(5), .dataWidth(32)) rom_21 (.addr(multiplexer_1_out), .data(out_23));  // open: sel
  ROM #(.addrWidth(5), .dataWidth(32)) rom_22 (.addr(multiplexer_1_out), .data(out_24));  // open: sel
  ROM #(.addrWidth(5), .dataWidth(32)) rom_23 (.addr(multiplexer_1_out), .data(out_25));  // open: sel
  ROM #(.addrWidth(5), .dataWidth(32)) rom_24 (.addr(multiplexer_1_out), .data(out_26));  // open: sel
  ROM #(.addrWidth(5), .dataWidth(32)) rom_25 (.addr(multiplexer_1_out), .data(out_27));  // open: sel
  ROM #(.addrWidth(5), .dataWidth(32)) rom_26 (.addr(multiplexer_1_out), .data(out_28));  // open: sel
  ROM #(.addrWidth(5), .dataWidth(32)) rom_27 (.addr(multiplexer_1_out), .data(out_29));  // open: sel
  ROM #(.addrWidth(5), .dataWidth(32)) rom_28 (.addr(multiplexer_1_out), .data(out_30));  // open: sel
  ROM #(.addrWidth(5), .dataWidth(32)) rom_29 (.addr(multiplexer_1_out), .data(out_31));  // open: sel
  ROM #(.addrWidth(5), .dataWidth(32)) rom_30 (.addr(multiplexer_1_out), .data(out_32));  // open: sel
  ROM #(.addrWidth(5), .dataWidth(32)) rom_31 (.addr(multiplexer_1_out), .data(out_33));  // open: sel
  ROM #(.addrWidth(5), .dataWidth(32)) rom_32 (.addr(multiplexer_1_out), .data(out_34));  // open: sel

  // Notes on the sheet:
  //   contents of rom_8 (hex, n*v repeats v):
  //   ffff ffff
  //   contents of rom_9 (hex, n*v repeats v):
  //   ffd555 3ffd555
  //   contents of rom_10 (hex, n*v repeats v):
  //   7ffdddd 1fffdddd
  //   contents of rom_11 (hex, n*v repeats v):
  //   fffdddd 3fffdddd
  //   contents of rom_12 (hex, n*v repeats v):
  //   1f00dddd 7c00dddd
  //   contents of rom_13 (hex, n*v repeats v):
  //   3c00dddd f000dddd
  //   contents of rom_14 (hex, n*v repeats v):
  //   3800dddd e000dddd
  //   contents of rom_15 (hex, n*v repeats v):
  //   3800dddd e000dddd
  //   contents of rom_16 (hex, n*v repeats v):
  //   3800dddd e000dddd
  //   contents of rom_17 (hex, n*v repeats v):
  //   3800dddd e000dddd
  //   contents of rom_18 (hex, n*v repeats v):
  //   3800dddd e000dddd
  //   contents of rom_19 (hex, n*v repeats v):
  //   3c00dddd f000dddd
  //   contents of rom_20 (hex, n*v repeats v):
  //   1f00dddd 7c00dddd
  //   contents of rom_21 (hex, n*v repeats v):
  //   fffdddd 3ffcdddd
  //   contents of rom_22 (hex, n*v repeats v):
  //   7ffdddd 1ffcdddd
  //   contents of rom_23 (hex, n*v repeats v):
  //   ffd555 3fcd555
  //   contents of rom_24 (hex, n*v repeats v):
  //   ffff ffff
endmodule

module PopCount (
  input  A,
  input  B,
  input  C,
  input  D,
  output X1,
  output X0
);

  wire and_1_out, and_2_out, and_3_out, and_4_out, and_5_out, and_6_out, and_7_out, and_8_out, and_9_out,
       not_1_out, not_2_out, not_3_out, not_4_out, or_1_out, or_2_out, or_3_out, xor_1_out;

  not not_1 (not_1_out, D);
  not not_2 (not_2_out, C);
  not not_3 (not_3_out, B);
  and and_1 (and_1_out, A, D);
  and and_2 (and_2_out, A, C);
  and and_3 (and_3_out, C, D);
  and and_4 (and_4_out, not_1_out, not_2_out);
  or or_1 (or_1_out, and_4_out, and_5_out);
  and and_5 (and_5_out, C, D);
  xor xor_1 (xor_1_out, C, D);
  or or_2 (or_2_out, xor_1_out, and_6_out);
  and and_6 (and_6_out, not_3_out, C);
  or or_3 (or_3_out, and_1_out, and_2_out);
  and and_7 (and_7_out, and_3_out, B);
  and and_8 (and_8_out, A, or_1_out);
  not not_4 (not_4_out, A);
  or or_4 (X1, or_3_out, and_7_out);
  or or_5 (X0, and_8_out, and_9_out);
  and and_9 (and_9_out, or_2_out, not_4_out);
endmodule

module LockDetect (
  input  A,
  input  B,
  input  C,
  input  D,
  output Y
);

  wire and_1_out, and_2_out, not_1_out;

  not not_1 (not_1_out, B);
  and and_1 (and_1_out, A, not_1_out);
  and and_2 (and_2_out, C, D);
  and and_3 (Y, and_1_out, and_2_out);
endmodule
