// Logisim project lab10part2.circ as structural Verilog: 3 circuits, main circuit main
module main (
  input  [3:0] in_1,
  output X0,
  output X1,
  output X2
);

  ParityGen paritygen_1 (.ABCD(in_1), .X0(X0), .X1(X1), .X2(X2));
endmodule

module GrayCode (
  input  [3:0] \input ,
  output X2,
  output X1,
  output X0
);
endmodule

module ParityGen (
  input  [3:0] ABCD,
  output X0,
  output X1,
  output X2
);

  xor xor_1 (X0, ABCD[0], ABCD[1]);
  xor xor_2 (X1, ABCD[1], ABCD[2]);
  xor xor_3 (X2, ABCD[2], ABCD[3]);
endmodule
