// Logisim project lab11part1.circ as structural Verilog: 1 circuit, main circuit main
module main (
  input  W_EN,
  input  [1:0] WriteRegister,
  input  [15:0] WriteData,
  input  [1:0] ReadRegister_1,
  input  [1:0] ReadRegister_2,
  output [15:0] ReadData_1,
  output [15:0] ReadData_2
);

  wire and_1_out, and_2_out, and_3_out, and_4_out, clock_1_out, decoder_1_out0, decoder_1_out1,
       decoder_1_out2, decoder_1_out3;
  wire [15:0] register_1_q, register_2_q, register_3_q, register_4_q;

  Decoder #(.select(2), .enable("false")) decoder_1 (
    .out0(decoder_1_out0), .out1(decoder_1_out1), .out2(decoder_1_out2), .out3(decoder_1_out3),
    .sel(WriteRegister));
  and and_1 (and_1_out, W_EN, decoder_1_out0);
  and and_2 (and_2_out, W_EN, decoder_1_out1);
  and and_3 (and_3_out, W_EN, decoder_1_out2);
  and and_4 (and_4_out, W_EN, decoder_1_out3);
  Clock clock_1 (.out(clock_1_out));
  Register #(.width(16)) register_1 (.D(WriteData), .en(and_1_out), .Q(register_1_q), .clk(clock_1_out));  // open: clr
  Register #(.width(16)) register_2 (.D(WriteData), .en(and_2_out), .Q(register_2_q), .clk(clock_1_out));  // open: clr
  Register #(.width(16)) register_3 (.D(WriteData), .en(and_3_out), .Q(register_3_q), .clk(clock_1_out));  // open: clr
  Register #(.width(16)) register_4 (.D(WriteData), .en(and_4_out), .Q(register_4_q), .clk(clock_1_out));  // open: clr
  Multiplexer #(.select(2), .width(16), .enable("false")) multiplexer_1 (
    .in0(register_1_q), .in1(register_2_q), .in2(register_3_q), .in3(register_4_q), .out(ReadData_1),
    .sel(ReadRegister_1));
  Multiplexer #(.select(2), .width(16), .enable("false")) multiplexer_2 (
    .in0(register_1_q), .in1(register_2_q), .in2(register_3_q), .in3(register_4_q), .out(ReadData_2),
    .sel(ReadRegister_2));
endmodule
