// Logisim project lab11part2.circ as structural Verilog: 1 circuit, main circuit main
module main (
);

  wire button_1_out, button_2_out, clock_1_out, not_1_out, not_2_out;
  wire [7:0] ram_1_data;
  wire [8:0] counter_1_q;

  Clock clock_1 (.out(clock_1_out));
  Counter #(.width(9), .max('h1ff), .ongoal("continue")) counter_1 (
    .count(not_1_out), .Q(counter_1_q), .clk(clock_1_out), .clr(button_1_out));  // open: load, D, carry
  Button button_1 (.out(button_1_out));
  not not_1 (not_1_out, counter_1_q[8]);
  RAM ram_1 (
    .addr(counter_1_q[7:0]), .data(ram_1_data), .sel(not_1_out), .clk(clock_1_out), .ld(not_2_out),
    .clr(button_2_out));
  Button button_2 (.out(button_2_out));
  not not_2 (not_2_out, not_1_out);
  assign ram_1_data = not_1_out ? 8'h61 : 8'bz;  // Controlled_Buffer controlled_buffer_1
endmodule
