// Logisim project lab12part1.circ as structural Verilog: 1 circuit, main circuit main
module main (
  input  A,
  output Z
);

  wire and_1_out, and_2_out, and_3_out, and_4_out, and_5_out, and_6_out, and_7_out, clock_1_out, D0_q, D0_qn,
       D1_q, D1_qn, D2_q, D2_qn, not_1_out, or_1_out, or_2_out, Reset_out, xor_1_out;

  not not_1 (not_1_out, A);
  and and_1 (and_1_out, not_1_out, D2_q);
  and and_2 (and_2_out, D1_q, D0_qn);
  and and_3 (and_3_out, A, D0_qn, D1_qn);
  and and_4 (and_4_out, A, D1_qn, D2_qn);
  Clock clock_1 (.out(clock_1_out));
  and and_5 (and_5_out, not_1_out, D2_q, D0_qn);
  and and_6 (and_6_out, A, D1_q, D0_q);
  or or_1 (or_1_out, and_5_out, and_6_out);
  xor xor_1 (xor_1_out, D1_q, D0_q);
  and and_7 (and_7_out, xor_1_out, A);
  or or_2 (or_2_out, and_1_out, and_2_out, and_3_out, and_4_out);
  D_Flip_Flop D2 (.clk(clock_1_out), .D(or_1_out), .Q(D2_q), .Qn(D2_qn), .reset(Reset_out));  // open: preset, en
  D_Flip_Flop D1 (.clk(clock_1_out), .D(and_7_out), .Q(D1_q), .Qn(D1_qn), .reset(Reset_out));  // open: preset, en
  D_Flip_Flop D0 (.clk(clock_1_out), .D(or_2_out), .Q(D0_q), .Qn(D0_qn), .reset(Reset_out));  // open: preset, en
  Button Reset (.out(Reset_out));
  and and_8 (Z, A, D2_q, D1_qn, D0_q);
endmodule
