// Logisim project jrmips.circ as structural Verilog: 17 circuits, main circuit main
module main (
  output [15:0] Read_1_Value,
  output [15:0] Read_2_Value,
  output [15:0] ALU_Out
);

  wire and_1_out, b_j_1_branch, b_j_1_jump, branch_check_1_branch_check, CLK_out, comparator_1_eq,
       comparator_2_eq, get_subop_1_subop, halt_dispenable_1_dispenable, halt_dispenable_1_halt, not_1_out,
       not_2_out, or_1_out, w_en_1_w_en;
  wire [1:0] alu_lw_pc_1_alu_lw_pc, get_low_two_1_branch_sel, im_shamt_reg_1_im_shamt_reg;
  wire [2:0] op_sel_1_op_sel, r_split_1_rs, r_split_1_rt;
  wire [3:0] r_split_1_shamt;
  wire [4:0] r_split_1_opcode;
  wire [7:0] adder_1_out, get_address_1_adr_8, get_low_8_1_low_8, i_split_1_im, multiplexer_1_out,
       multiplexer_2_out, PC_q;
  wire [15:0] bit_extender_1_out, bit_extender_2_out, demultiplexer_1_out0, demultiplexer_1_out1, DispOut_q,
       extend_im_1_s_ext, extend_im_1_z_ext, multiplexer_3_out, multiplexer_4_out, multiplexer_5_out,
       ram_1_data, rom_1_data;

  Clock CLK (.out(CLK_out));
  or or_1 (or_1_out, b_j_1_jump, and_1_out);
  Adder adder_1 (.a(PC_q), .b(8'h1), .out(adder_1_out));  // open: cin, cout
  and and_1 (and_1_out, branch_check_1_branch_check, b_j_1_branch);
  Register PC (.D(multiplexer_1_out), .en(not_1_out), .Q(PC_q), .clk(CLK_out));  // open: clr
  Multiplexer #(.width(8), .enable("false")) multiplexer_1 (
    .in0(adder_1_out), .in1(multiplexer_2_out), .out(multiplexer_1_out), .sel(or_1_out));
  Multiplexer #(.width(8), .enable("false")) multiplexer_2 (
    .in0(i_split_1_im), .in1(get_low_8_1_low_8), .out(multiplexer_2_out), .sel(comparator_1_eq));
  Branch_Check branch_check_1 (
    .Branch_Sel(get_low_two_1_branch_sel), .Rs(Read_1_Value), .Branch_Check(branch_check_1_branch_check));
  Get_Low_8 get_low_8_1 (.Reg_1_Value(Read_1_Value), .Low_8(get_low_8_1_low_8));
  not not_1 (not_1_out, halt_dispenable_1_halt);
  assign bit_extender_1_out = {{8{1'b0}}, PC_q};  // Bit_Extender bit_extender_1
  Comparator #(.width(5)) comparator_1 (.a(r_split_1_opcode), .b(5'b11100), .eq(comparator_1_eq));  // open: gt, lt
  B_J b_j_1 (.OpCode_SubOp(r_split_1_opcode), .Branch(b_j_1_branch), .Jump(b_j_1_jump));
  Get_Low_Two get_low_two_1 (.OpCode(r_split_1_opcode), .Branch_Sel(get_low_two_1_branch_sel));
  ROM #(.dataWidth(16)) rom_1 (.addr(PC_q), .data(rom_1_data));  // open: sel
  Get_SubOp get_subop_1 (.Instr_In(rom_1_data), .SubOp(get_subop_1_subop));
  not not_2 (not_2_out, get_subop_1_subop);
  R_Split r_split_1 (
    .Instr_In(rom_1_data), .OpCode(r_split_1_opcode), .Rs(r_split_1_rs), .Rt(r_split_1_rt),
    .Shamt(r_split_1_shamt));
  I_Split i_split_1 (.Instr_In(rom_1_data), .Im(i_split_1_im));  // open: OpCode, Rs
  Extend_Im extend_im_1 (.Im_In(i_split_1_im), .Z_Ext(extend_im_1_z_ext), .S_Ext(extend_im_1_s_ext));
  Multiplexer #(.width(16), .enable("false")) multiplexer_3 (
    .in0(extend_im_1_z_ext), .in1(extend_im_1_s_ext), .out(multiplexer_3_out), .sel(get_subop_1_subop));
  Demultiplexer #(.width(16), .enable("false")) demultiplexer_1 (
    .out0(demultiplexer_1_out0), .out1(demultiplexer_1_out1), .in(Read_2_Value), .sel(get_subop_1_subop));
  Comparator #(.width(5)) comparator_2 (.a(r_split_1_opcode), .b(5'b01111), .eq(comparator_2_eq));  // open: gt, lt
  Op_Sel op_sel_1 (.OpCode_SubOp(r_split_1_opcode), .Op_Sel(op_sel_1_op_sel));
  Im_Shamt_Reg im_shamt_reg_1 (.OpCode_SubOp(r_split_1_opcode), .Im_Shamt_Reg(im_shamt_reg_1_im_shamt_reg));
  W_EN w_en_1 (.OpCode_SubOp(r_split_1_opcode), .W_EN(w_en_1_w_en));
  assign bit_extender_2_out = {{12{1'b0}}, r_split_1_shamt};  // Bit_Extender bit_extender_2
  Multiplexer #(.select(2), .width(16), .enable("false")) multiplexer_4 (
    .in0(multiplexer_3_out), .in1(bit_extender_2_out), .in2(Read_2_Value), .out(multiplexer_4_out),
    .sel(im_shamt_reg_1_im_shamt_reg));  // open: in3
  Get_Address get_address_1 (.Adr_16(demultiplexer_1_out0), .Adr_8(get_address_1_adr_8));
  ALU_LW_PC alu_lw_pc_1 (.OpCode_SubOp(r_split_1_opcode), .ALU_LW_PC(alu_lw_pc_1_alu_lw_pc));
  RegisterFile registerfile_1 (
    .W_EN(w_en_1_w_en), .WriteRegister(r_split_1_rs), .WriteData(multiplexer_5_out),
    .ReadRegister_1(r_split_1_rs), .ReadRegister_2(r_split_1_rt), .CLK(CLK_out), .ReadData_1(Read_1_Value),
    .ReadData_2(Read_2_Value));
  ALU alu_1 (.Op_Sel(op_sel_1_op_sel), .RS(Read_1_Value), .RT(multiplexer_4_out), .ALU_Out(ALU_Out));
  RAM #(.dataWidth(16), .bus("separate")) ram_1 (
    .addr(get_address_1_adr_8), .din(demultiplexer_1_out1), .data(ram_1_data), .str(comparator_2_eq),
    .sel(1'b1), .clk(CLK_out), .ld(not_2_out));  // open: clr
  Halt_DispEnable halt_dispenable_1 (
    .OpCode_SubOp(r_split_1_opcode), .HALT(halt_dispenable_1_halt), .DispEnable(halt_dispenable_1_dispenable));
  Multiplexer #(.select(2), .width(16), .enable("false")) multiplexer_5 (
    .in0(ALU_Out), .in1(ram_1_data), .in2(bit_extender_1_out), .out(multiplexer_5_out),
    .sel(alu_lw_pc_1_alu_lw_pc));  // open: in3
  Register #(.width(16)) DispOut (
    .D(Read_1_Value), .en(halt_dispenable_1_dispenable), .Q(DispOut_q), .clk(CLK_out));  // open: clr
  Hex_Digit_Display hex_digit_display_1 (.value(DispOut_q[15:12]));  // open: dp
  LED HALT (.in(halt_dispenable_1_halt));
  Hex_Digit_Display hex_digit_display_2 (.value(DispOut_q[7:4]));  // open: dp
  Hex_Digit_Display hex_digit_display_3 (.value(DispOut_q[11:8]));  // open: dp
  Hex_Digit_Display hex_digit_display_4 (.value(DispOut_q[3:0]));  // open: dp

  // Notes on the sheet:
  //   Steve Comer
  //   sfc15@pitt.edu
  //   From Control (branch/jump)
  //   contents of rom_1 (hex, n*v repeats v):
  //   403 80b 7501 7f00 ce00 e03 7f01 7d00 cc00 803 c03 7d01 803 c03 7d01 60d 7ec0 ce00 603 7ec0 ce00 2001
  //   OpCode
  //   Im_Shamt_Reg
  //   Op_Sel
  //   I_S_R
  //   W_EN
  //   A_L_P
  //   Halt_DispEnable
  //   ALU_LW_PC
endmodule

// RegFile
module RegisterFile (
  input  W_EN,
  input  [2:0] WriteRegister,
  input  [15:0] WriteData,
  input  [2:0] ReadRegister_1,
  input  [2:0] ReadRegister_2,
  input  CLK,
  output [15:0] ReadData_1,
  output [15:0] ReadData_2
);

  wire and_1_out, and_2_out, and_3_out, and_4_out, and_5_out, and_6_out, and_7_out, and_8_out,
       decoder_1_out0, decoder_1_out1, decoder_1_out2, decoder_1_out3, decoder_1_out4, decoder_1_out5,
       decoder_1_out6, decoder_1_out7;
  wire [15:0] register_1_q, register_2_q, register_3_q, register_4_q, register_5_q, register_6_q,
       register_7_q, register_8_q;

  Decoder #(.select(3), .enable("false")) decoder_1 (
    .out0(decoder_1_out0), .out1(decoder_1_out1), .out2(decoder_1_out2), .out3(decoder_1_out3),
    .out4(decoder_1_out4), .out5(decoder_1_out5), .out6(decoder_1_out6), .out7(decoder_1_out7),
    .sel(WriteRegister));
  and and_1 (and_1_out, W_EN, decoder_1_out0);
  and and_2 (and_2_out, W_EN, decoder_1_out1);
  and and_3 (and_3_out, W_EN, decoder_1_out2);
  and and_4 (and_4_out, W_EN, decoder_1_out3);
  and and_5 (and_5_out, W_EN, decoder_1_out4);
  and and_6 (and_6_out, W_EN, decoder_1_out5);
  and and_7 (and_7_out, W_EN, decoder_1_out6);
  and and_8 (and_8_out, W_EN, decoder_1_out7);
  Register #(.width(16)) register_1 (.D(WriteData), .en(and_1_out), .Q(register_1_q), .clk(CLK));  // open: clr
  Register #(.width(16)) register_2 (.D(WriteData), .en(and_2_out), .Q(register_2_q), .clk(CLK));  // open: clr
  Register #(.width(16)) register_3 (.D(WriteData), .en(and_3_out), .Q(register_3_q), .clk(CLK));  // open: clr
  Register #(.width(16)) register_4 (.D(WriteData), .en(and_4_out), .Q(register_4_q), .clk(CLK));  // open: clr
  Register #(.width(16)) register_5 (.D(WriteData), .en(and_5_out), .Q(register_5_q), .clk(CLK));  // open: clr
  Register #(.width(16)) register_6 (.D(WriteData), .en(and_6_out), .Q(register_6_q), .clk(CLK));  // open: clr
  Register #(.width(16)) register_7 (.D(WriteData), .en(and_7_out), .Q(register_7_q), .clk(CLK));  // open: clr
  Register #(.width(16)) register_8 (.D(WriteData), .en(and_8_out), .Q(register_8_q), .clk(CLK));  // open: clr
  Multiplexer #(.select(3), .width(16), .enable("false")) multiplexer_1 (
    .in0(register_1_q), .in1(register_2_q), .in2(register_3_q), .in3(register_4_q), .in4(register_5_q),
    .in5(register_6_q), .in6(register_7_q), .in7(register_8_q), .out(ReadData_1), .sel(ReadRegister_1));
  Multiplexer #(.select(3), .width(16), .enable("false")) multiplexer_2 (
    .in0(register_1_q), .in1(register_2_q), .in2(register_3_q), .in3(register_4_q), .in4(register_5_q),
    .in5(register_6_q), .in6(register_7_q), .in7(register_8_q), .out(ReadData_2), .sel(ReadRegister_2));
endmodule

module ALU (
  input  [2:0] Op_Sel,
  input  [15:0] RS,
  input  [15:0] RT,
  output [15:0] ALU_Out
);

  wire [15:0] adder_1_out, and_1_out, nor_1_out, shifter_1_out, shifter_2_out, subtractor_1_out;

  Adder #(.width(16)) adder_1 (.a(RS), .b(RT), .out(adder_1_out));  // open: cin, cout
  Subtractor #(.width(16)) subtractor_1 (.a(RS), .b(RT), .out(subtractor_1_out));  // open: bin, bout
  assign and_1_out = RS & RT;  // AND_Gate and_1, 16 bits wide
  assign nor_1_out = ~(RS | RT);  // NOR_Gate nor_1, 16 bits wide
  Shifter #(.width(16)) shifter_1 (.in(RS), .\dist (RT[3:0]), .out(shifter_1_out));
  Shifter #(.width(16), .shift("lr")) shifter_2 (.in(RS), .\dist (RT[3:0]), .out(shifter_2_out));
  Multiplexer #(.select(3), .width(16)) multiplexer_1 (
    .in0(adder_1_out), .in1(subtractor_1_out), .in2(and_1_out), .in3(nor_1_out), .in4(shifter_1_out),
    .in5(shifter_2_out), .out(ALU_Out), .sel(Op_Sel));  // open: in6, in7, en
endmodule

// I
module I_Split (
  input  [15:0] Instr_In,
  output [4:0] OpCode,
  output [2:0] Rs,
  output [7:0] Im
);


  assign Im = Instr_In[8:1];
  assign OpCode = {Instr_In[15:12], Instr_In[0]};
  assign Rs = Instr_In[11:9];
endmodule

// R
module R_Split (
  input  [15:0] Instr_In,
  output [4:0] OpCode,
  output [2:0] Rs,
  output [2:0] Rt,
  output [3:0] Shamt
);


  assign OpCode = {Instr_In[15:12], Instr_In[0]};
  assign Rs = Instr_In[11:9];
  assign Rt = Instr_In[8:6];
  assign Shamt = Instr_In[4:1];
endmodule

// SubOp
module Get_SubOp (
  input  [15:0] Instr_In,
  output SubOp
);


  assign SubOp = Instr_In[0];
endmodule

// Im
module Extend_Im (
  input  [7:0] Im_In,
  output [15:0] Z_Ext,
  output [15:0] S_Ext
);

  assign Z_Ext = {{8{1'b0}}, Im_In};  // Bit_Extender bit_extender_1
  assign S_Ext = {{8{Im_In[7]}}, Im_In};  // Bit_Extender bit_extender_2
endmodule

module Get_Address (
  input  [15:0] Adr_16,
  output [7:0] Adr_8
);


  assign Adr_8 = Adr_16[7:0];
endmodule

module Halt_DispEnable (
  input  [4:0] OpCode_SubOp,
  output HALT,
  output DispEnable
);

  wire not_1_out, not_2_out, not_3_out, not_4_out, not_5_out;

  not not_1 (not_1_out, OpCode_SubOp[4]);
  not not_2 (not_2_out, OpCode_SubOp[3]);
  not not_3 (not_3_out, OpCode_SubOp[1]);
  not not_4 (not_4_out, OpCode_SubOp[2]);
  not not_5 (not_5_out, OpCode_SubOp[1]);
  and and_1 (HALT, not_1_out, not_2_out, OpCode_SubOp[2], not_3_out, OpCode_SubOp[0]);
  and and_2 (DispEnable, OpCode_SubOp[4], OpCode_SubOp[3], not_4_out, not_5_out);
endmodule

module W_EN (
  input  [4:0] OpCode_SubOp,
  output W_EN
);

  wire and_1_out, and_2_out, and_3_out, and_4_out, and_5_out, and_6_out, not_1_out, not_2_out, not_3_out,
       not_4_out, not_5_out, not_6_out, not_7_out;

  not not_1 (not_1_out, OpCode_SubOp[4]);
  not not_2 (not_2_out, OpCode_SubOp[2]);
  not not_3 (not_3_out, OpCode_SubOp[4]);
  not not_4 (not_4_out, OpCode_SubOp[1]);
  not not_5 (not_5_out, OpCode_SubOp[4]);
  not not_6 (not_6_out, OpCode_SubOp[0]);
  not not_7 (not_7_out, OpCode_SubOp[3]);
  and and_1 (and_1_out, not_1_out, not_2_out);
  and and_2 (and_2_out, not_3_out, not_4_out);
  and and_3 (and_3_out, not_5_out, not_6_out);
  and and_4 (and_4_out, not_7_out, OpCode_SubOp[2]);
  and and_5 (and_5_out, OpCode_SubOp[4], OpCode_SubOp[2], OpCode_SubOp[0]);
  and and_6 (and_6_out, OpCode_SubOp[4], OpCode_SubOp[3], OpCode_SubOp[1]);
  or or_1 (W_EN, and_1_out, and_2_out, and_3_out, and_4_out, and_5_out, and_6_out);
endmodule

module Im_Shamt_Reg (
  input  [4:0] OpCode_SubOp,
  output [1:0] Im_Shamt_Reg
);

  wire and_1_out, and_2_out, not_1_out, not_2_out;

  not not_1 (not_1_out, OpCode_SubOp[3]);
  not not_2 (not_2_out, OpCode_SubOp[0]);
  and and_1 (and_1_out, not_1_out, OpCode_SubOp[1]);
  and and_2 (and_2_out, OpCode_SubOp[3], OpCode_SubOp[0]);
  and and_3 (Im_Shamt_Reg[0], OpCode_SubOp[3], not_2_out);
  or or_1 (Im_Shamt_Reg[1], and_1_out, and_2_out);
endmodule

module Op_Sel (
  input  [4:0] OpCode_SubOp,
  output [2:0] Op_Sel
);

  wire and_3_out, and_4_out, not_1_out, not_2_out, not_3_out, not_4_out, not_5_out, not_6_out, not_7_out,
       not_8_out;

  not not_1 (not_1_out, OpCode_SubOp[4]);
  not not_2 (not_2_out, OpCode_SubOp[2]);
  not not_3 (not_3_out, OpCode_SubOp[4]);
  not not_4 (not_4_out, OpCode_SubOp[3]);
  not not_5 (not_5_out, OpCode_SubOp[4]);
  not not_6 (not_6_out, OpCode_SubOp[3]);
  not not_7 (not_7_out, OpCode_SubOp[4]);
  not not_8 (not_8_out, OpCode_SubOp[2]);
  and and_1 (Op_Sel[2], not_1_out, OpCode_SubOp[3], not_2_out);
  and and_2 (Op_Sel[1], not_3_out, not_4_out, OpCode_SubOp[2], OpCode_SubOp[1]);
  and and_3 (and_3_out, not_5_out, not_6_out, OpCode_SubOp[1], OpCode_SubOp[0]);
  and and_4 (and_4_out, not_7_out, OpCode_SubOp[3], not_8_out, OpCode_SubOp[1]);
  or or_1 (Op_Sel[0], and_3_out, and_4_out);
endmodule

module ALU_LW_PC (
  input  [4:0] OpCode_SubOp,
  output [1:0] ALU_LW_PC
);

  wire not_1_out, not_2_out, not_3_out;

  not not_1 (not_1_out, OpCode_SubOp[1]);
  not not_2 (not_2_out, OpCode_SubOp[4]);
  not not_3 (not_3_out, OpCode_SubOp[0]);
  and and_1 (ALU_LW_PC[1], OpCode_SubOp[4], OpCode_SubOp[3], OpCode_SubOp[2], not_1_out, OpCode_SubOp[0]);
  and and_2 (ALU_LW_PC[0], not_2_out, OpCode_SubOp[3], OpCode_SubOp[2], OpCode_SubOp[1], not_3_out);
endmodule

module Branch_Check (
  input  [1:0] Branch_Sel,
  input  [15:0] Rs,
  output Branch_Check
);

  wire comparator_1_eq, comparator_1_gt, comparator_1_lt, not_1_out;

  Comparator #(.width(16)) comparator_1 (
    .a(Rs), .b({16{1'b0}}), .gt(comparator_1_gt), .eq(comparator_1_eq), .lt(comparator_1_lt));
  not not_1 (not_1_out, comparator_1_eq);
  Multiplexer #(.select(2), .enable("false")) multiplexer_1 (
    .in0(comparator_1_lt), .in1(comparator_1_gt), .in2(not_1_out), .in3(comparator_1_eq), .out(Branch_Check),
    .sel(Branch_Sel));
endmodule

module B_J (
  input  [4:0] OpCode_SubOp,
  output Branch,
  output Jump
);

  wire and_2_out, and_3_out, not_1_out, not_2_out, not_3_out, not_4_out;

  not not_1 (not_1_out, OpCode_SubOp[3]);
  not not_2 (not_2_out, OpCode_SubOp[2]);
  not not_3 (not_3_out, OpCode_SubOp[2]);
  not not_4 (not_4_out, OpCode_SubOp[1]);
  and and_1 (Branch, OpCode_SubOp[4], not_1_out, not_2_out);
  and and_2 (and_2_out, OpCode_SubOp[4], OpCode_SubOp[3], not_3_out, OpCode_SubOp[1]);
  and and_3 (and_3_out, OpCode_SubOp[4], OpCode_SubOp[3], OpCode_SubOp[2], not_4_out);
  or or_1 (Jump, and_2_out, and_3_out);
endmodule

module Get_Low_Two (
  input  [4:0] OpCode,
  output [1:0] Branch_Sel
);


  assign Branch_Sel = OpCode[1:0];
endmodule

module Get_Low_8 (
  input  [15:0] Reg_1_Value,
  output [7:0] Low_8
);


  assign Low_8 = Reg_1_Value[7:0];
endmodule
